// Logisim project saguiLongo.circ as structural Verilog: 7 circuits, main circuit main
module main (
);

  wire Clk, memWrite, not_1_out;
  wire [1:0] data_FU_selector;
  wire [2:0] arith1_FU_selector, arith2_FU_selector, ctrl_FU_selector;
  wire [4:0] control_unit_1_arithm1, control_unit_1_arithm2, control_unit_1_ctrl, control_unit_1_data;
  wire [7:0] adder_1_out, arithmetic_type_fu_1_result, arithmetic_type_fu_2_result,
       bancoregistradores_1_arithm1_a, bancoregistradores_1_arithm1_b, bancoregistradores_1_arithm2_a,
       bancoregistradores_1_arithm2_b, bancoregistradores_1_ctrl_a, bancoregistradores_1_ctrl_b,
       bancoregistradores_1_data_a, bancoregistradores_1_data_b, ctrl_type_fu_1_pc_out,
       data_type_fu_1_result, multiplexer_1_out, PC_q, ram_1_dout, rom_1_p2, rom_1_p3, rom_1_p4, rom_1_p5;

  Adder adder_1 (.a(PC_q), .b(8'h4), .out(adder_1_out), .cin(1'b0));  // open: cout
  Multiplexer #(.width(8)) multiplexer_1 (
    .in0(adder_1_out), .in1(ctrl_type_fu_1_pc_out), .out(multiplexer_1_out), .sel(1'b0));
  Register PC (.D(multiplexer_1_out), .en(1'b1), .clk(Clk), .Q(PC_q), .clr(1'b0));
  // ROM #(.line("quad")) rom_1: pin names not known; wires that end beside it: PC_q, rom_1_p2, rom_1_p3, rom_1_p4, rom_1_p5
  Clock clock_Global (.out(Clk));
  Control_unit control_unit_1 (
    .i_00(rom_1_p2), .i_01(rom_1_p3), .i_02(rom_1_p4), .i_03(rom_1_p5), .data(control_unit_1_data),
    .arithm1(control_unit_1_arithm1), .arithm2(control_unit_1_arithm2), .ctrl(control_unit_1_ctrl));  // open: data_FU_selector, arith1_FU_selector, arith2_FU_selector, ctrl_FU_selector
  BancoRegistradores bancoregistradores_1 (
    .WD_data(ram_1_dout), .WD_arith1(arithmetic_type_fu_1_result), .WD_arith2(arithmetic_type_fu_2_result),
    .data(control_unit_1_data), .arithm1(control_unit_1_arithm1), .arithm2(control_unit_1_arithm2),
    .ctrl(control_unit_1_ctrl), .data_a(bancoregistradores_1_data_a), .data_b(bancoregistradores_1_data_b),
    .arithm1_a(bancoregistradores_1_arithm1_a), .arithm1_b(bancoregistradores_1_arithm1_b),
    .arithm2_a(bancoregistradores_1_arithm2_a), .arithm2_b(bancoregistradores_1_arithm2_b),
    .ctrl_a(bancoregistradores_1_ctrl_a), .ctrl_b(bancoregistradores_1_ctrl_b));  // open: clk
  RAM #(.asyncread("true")) ram_1 (
    .addr(bancoregistradores_1_data_a), .we(memWrite), .oe(not_1_out), .clk(Clk),
    .din(data_type_fu_1_result), .dout(ram_1_dout));
  not not_1 (not_1_out, memWrite);
  Data_type_FU data_type_fu_1 (
    .a(bancoregistradores_1_data_a), .b(bancoregistradores_1_data_b), .selector(data_FU_selector),
    .result(data_type_fu_1_result));
  Arithmetic_type_FU arithmetic_type_fu_1 (
    .a(bancoregistradores_1_arithm1_a), .b(bancoregistradores_1_arithm1_b), .selector(arith1_FU_selector),
    .result(arithmetic_type_fu_1_result));
  Arithmetic_type_FU arithmetic_type_fu_2 (
    .a(bancoregistradores_1_arithm2_a), .b(bancoregistradores_1_arithm2_b), .selector(arith2_FU_selector),
    .result(arithmetic_type_fu_2_result));
  Ctrl_type_FU ctrl_type_fu_1 (
    .a(bancoregistradores_1_ctrl_a), .b(bancoregistradores_1_ctrl_b), .PC_in(PC_q),
    .selector(ctrl_FU_selector), .PC_out(ctrl_type_fu_1_pc_out));

  // Notes on the sheet:
  //   Memoria de Instrucoes
  //   Memoria de Dados
endmodule

module Data_type_FU (
  input  [7:0] a,
  input  [7:0] b,
  input  [1:0] selector,
  output [7:0] result
);

  wire [3:0] bit_extender_1_out;

  Bit_Extender #(.out_width(4)) bit_extender_1 (.in(b), .out(bit_extender_1_out));
  Multiplexer #(.select(2), .width(8)) multiplexer_1 (
    .in0({bit_extender_1_out, a[3:0]}), .in1({a[7:4], bit_extender_1_out}), .in2(b), .in3({8{1'b0}}),
    .out(result), .sel(selector));

  // Notes on the sheet:
  //   Move High
  //   Move Low
  //   Ld/St address
endmodule

module Arithmetic_type_FU (
  input  [7:0] a,
  input  [7:0] b,
  input  [2:0] selector,
  output [7:0] result
);

  wire or_2_out;
  wire [7:0] adder_1_out, and_1_out, multiplexer_1_out, multiplexer_2_out, not_1_out, or_1_out,
       shifter_1_out, shifter_2_out, subtractor_1_out;

  Adder adder_1 (.a(a), .b(b), .out(adder_1_out), .cin(1'b0));  // open: cout
  Subtractor subtractor_1 (.a(a), .b(b), .out(subtractor_1_out), .bin(1'b0));  // open: bout
  assign and_1_out = a & b;  // AND_Gate and_1, 8 bits wide
  assign or_1_out = a | b;  // OR_Gate or_1, 8 bits wide
  assign not_1_out = ~b;  // NOT_Gate not_1, 8 bits wide
  Shifter shifter_1 (.in(a), .\dist (b[2:0]), .out(shifter_1_out));
  Shifter #(.shift("lr")) shifter_2 (.in(a), .\dist (b[2:0]), .out(shifter_2_out));
  Multiplexer #(.width(8)) multiplexer_1 (
    .in0(shifter_1_out), .in1({8{1'b0}}), .out(multiplexer_1_out), .sel(or_2_out));
  Multiplexer #(.width(8)) multiplexer_2 (
    .in0(shifter_2_out), .in1({8{1'b0}}), .out(multiplexer_2_out), .sel(or_2_out));
  or or_2 (or_2_out, b[7], b[6], b[5], b[4], b[3]);
  Multiplexer #(.select(3), .width(8)) multiplexer_3 (
    .in0(adder_1_out), .in1(subtractor_1_out), .in2(and_1_out), .in3(or_1_out), .in4(not_1_out),
    .in5(multiplexer_1_out), .in6(multiplexer_2_out), .in7({8{1'b0}}), .out(result), .sel(selector));

  // Notes on the sheet:
  //   Somador
  //   Subtrator
  //   And
  //   Or
  //   Not
  //   Logical Shifter Left
  //   Logical Shifter Right
endmodule

module Ctrl_type_FU (
  input  [7:0] a,
  input  [7:0] b,
  input  [7:0] PC_in,
  input  [2:0] selector,
  output [7:0] PC_out
);

  wire isZero;
  wire [7:0] adder_1_out, multiplexer_1_out, multiplexer_2_out;

  nor nor_1 (isZero, a[0], a[1], a[2], a[3], a[5], a[6], a[7], a[4]);
  Adder adder_1 (.a(b), .b(PC_in), .out(adder_1_out), .cin(1'b0));  // open: cout
  Multiplexer #(.width(8)) multiplexer_1 (.in0(PC_in), .in1(b), .out(multiplexer_1_out), .sel(isZero));
  Multiplexer #(.width(8)) multiplexer_2 (.in0(PC_in), .in1(adder_1_out), .out(multiplexer_2_out), .sel(isZero));
  Multiplexer #(.select(3), .width(8)) multiplexer_3 (
    .in0(b), .in1(adder_1_out), .in2(multiplexer_1_out), .in3(multiplexer_2_out), .out(PC_out), .sel(selector));  // open: in4, in5, in6, in7

  // Notes on the sheet:
  //   PC + Imm
  //   Jump Register
  //   Jump Immediate
  //   Branch On Zero Register
  //   Branch On Zero
endmodule

module BancoRegistradores (
  input  clk,
  input  [7:0] WD_data,
  input  [7:0] WD_arith1,
  input  [7:0] WD_arith2,
  input  [4:0] data,
  input  [4:0] arithm1,
  input  [4:0] arithm2,
  input  [4:0] ctrl,
  output [7:0] data_a,
  output [7:0] data_b,
  output [7:0] arithm1_a,
  output [7:0] arithm1_b,
  output [7:0] arithm2_a,
  output [7:0] arithm2_b,
  output [7:0] ctrl_a,
  output [7:0] ctrl_b
);

  wire not_1_out, not_2_out, not_3_out, xor_1_out, xor_2_out, xor_3_out, xor_4_out;
  wire [2:0] decoder_1_out0, decoder_1_out1, decoder_1_out2, decoder_1_out3;
  wire [7:0] multiplexer_1_out, multiplexer_2_out, multiplexer_3_out, multiplexer_4_out, register_1_q,
       register_2_q, register_3_q, register_4_q;

  not not_1 (not_1_out, data[4]);
  not not_2 (not_2_out, arithm1[4]);
  not not_3 (not_3_out, arithm2[4]);
  Decoder #(.select(2)) decoder_1 (
    .out0(decoder_1_out0[0]), .out1(decoder_1_out1[0]), .out2(decoder_1_out2[0]), .out3(decoder_1_out3[0]),
    .sel(data[1:0]), .en(not_1_out));
  Decoder #(.select(2)) decoder_2 (
    .out0(decoder_1_out0[1]), .out1(decoder_1_out1[1]), .out2(decoder_1_out2[1]), .out3(decoder_1_out3[1]),
    .sel(arithm1[1:0]), .en(not_2_out));
  Decoder #(.select(2)) decoder_3 (
    .out0(decoder_1_out0[2]), .out1(decoder_1_out1[2]), .out2(decoder_1_out2[2]), .out3(decoder_1_out3[2]),
    .sel(arithm2[1:0]), .en(not_3_out));
  Multiplexer #(.select(3), .width(8)) multiplexer_1 (
    .in0({8{1'b0}}), .in1(WD_data), .in2(WD_arith1), .in3({8{1'b0}}), .in4(WD_arith2), .in5({8{1'b0}}),
    .in6({8{1'b0}}), .in7({8{1'b0}}), .out(multiplexer_1_out), .sel(decoder_1_out0));
  ExactlyOne xor_1 (.out(xor_1_out), .in0(decoder_1_out0[0]), .in1(decoder_1_out0[1]), .in2(decoder_1_out0[2]));
  Multiplexer #(.select(3), .width(8)) multiplexer_2 (
    .in0({8{1'b0}}), .in1(WD_data), .in2(WD_arith1), .in3({8{1'b0}}), .in4(WD_arith2), .in5({8{1'b0}}),
    .in6({8{1'b0}}), .in7({8{1'b0}}), .out(multiplexer_2_out), .sel(decoder_1_out1));
  ExactlyOne xor_2 (.out(xor_2_out), .in0(decoder_1_out1[0]), .in1(decoder_1_out1[1]), .in2(decoder_1_out1[2]));
  Multiplexer #(.select(3), .width(8)) multiplexer_3 (
    .in0({8{1'b0}}), .in1(WD_data), .in2(WD_arith1), .in3({8{1'b0}}), .in4(WD_arith2), .in5({8{1'b0}}),
    .in6({8{1'b0}}), .in7({8{1'b0}}), .out(multiplexer_3_out), .sel(decoder_1_out2));
  ExactlyOne xor_3 (.out(xor_3_out), .in0(decoder_1_out2[0]), .in1(decoder_1_out2[1]), .in2(decoder_1_out2[2]));
  Multiplexer #(.select(3), .width(8)) multiplexer_4 (
    .in0({8{1'b0}}), .in1(WD_data), .in2(WD_arith1), .in3({8{1'b0}}), .in4(WD_arith2), .in5({8{1'b0}}),
    .in6({8{1'b0}}), .in7({8{1'b0}}), .out(multiplexer_4_out), .sel(decoder_1_out3));
  ExactlyOne xor_4 (.out(xor_4_out), .in0(decoder_1_out3[0]), .in1(decoder_1_out3[1]), .in2(decoder_1_out3[2]));
  Register register_1 (.D(multiplexer_1_out), .en(xor_1_out), .clk(clk), .Q(register_1_q), .clr(1'b0));
  Register register_2 (.D(multiplexer_2_out), .en(xor_2_out), .clk(clk), .Q(register_2_q), .clr(1'b0));
  Register register_3 (.D(multiplexer_3_out), .en(xor_3_out), .clk(clk), .Q(register_3_q), .clr(1'b0));
  Register register_4 (.D(multiplexer_4_out), .en(xor_4_out), .clk(clk), .Q(register_4_q), .clr(1'b0));
  Multiplexer #(.select(2), .width(8)) multiplexer_5 (
    .in0(register_1_q), .in1(register_2_q), .in2(register_3_q), .in3(register_4_q), .out(data_a),
    .sel(data[1:0]));
  Multiplexer #(.select(2), .width(8)) multiplexer_6 (
    .in0(register_1_q), .in1(register_2_q), .in2(register_3_q), .in3(register_4_q), .out(data_b),
    .sel(data[3:2]));
  Multiplexer #(.select(2), .width(8)) multiplexer_7 (
    .in0(register_1_q), .in1(register_2_q), .in2(register_3_q), .in3(register_4_q), .out(arithm1_a),
    .sel(arithm1[1:0]));
  Multiplexer #(.select(2), .width(8)) multiplexer_8 (
    .in0(register_1_q), .in1(register_2_q), .in2(register_3_q), .in3(register_4_q), .out(arithm1_b),
    .sel(arithm1[3:2]));
  Multiplexer #(.select(2), .width(8)) multiplexer_9 (
    .in0(register_1_q), .in1(register_2_q), .in2(register_3_q), .in3(register_4_q), .out(arithm2_a),
    .sel(arithm2[1:0]));
  Multiplexer #(.select(2), .width(8)) multiplexer_10 (
    .in0(register_1_q), .in1(register_2_q), .in2(register_3_q), .in3(register_4_q), .out(arithm2_b),
    .sel(arithm2[3:2]));
  Multiplexer #(.select(2), .width(8)) multiplexer_11 (
    .in0(register_1_q), .in1(register_2_q), .in2(register_3_q), .in3(register_4_q), .out(ctrl_a),
    .sel(ctrl[1:0]));
  Multiplexer #(.select(2), .width(8)) multiplexer_12 (
    .in0(register_1_q), .in1(register_2_q), .in2(register_3_q), .in3(register_4_q), .out(ctrl_b),
    .sel(ctrl[3:2]));

  // Other names for the same wires on the sheet: arithm1_a_address[1:0] = arithm1[1:0];
  //   arithm1_b_address[1:0] = arithm1[3:2]; arithm1_WE = arithm1[4]; arithm2_a_address[1:0] = arithm2[1:0];
  //   arithm2_b_address[1:0] = arithm2[3:2]; arithm2_WE = arithm2[4]; ctrl_a_address[1:0] = ctrl[1:0];
  //   ctrl_b_address[1:0] = ctrl[3:2]; ctrl_WE = ctrl[4]; data_a_address[1:0] = data[1:0];
  //   data_b_address[1:0] = data[3:2]; data_WE = data[4]
endmodule

module Control_unit (
  input  [7:0] i_00,
  input  [7:0] i_01,
  input  [7:0] i_02,
  input  [7:0] i_03,
  output [4:0] data,
  output [4:0] arithm1,
  output [4:0] arithm2,
  output [4:0] ctrl,
  output [1:0] data_FU_selector,
  output [2:0] arith1_FU_selector,
  output [2:0] arith2_FU_selector,
  output [1:0] ctrl_FU_selector
);

  wire [2:0] undriven;
  wire [7:0] rom_1_data;

  ROM #(.addrWidth(4)) rom_1 (.addr(i_00[7:4]), .data(rom_1_data));
  ROM #(.addrWidth(4)) rom_2 (.addr(i_01[7:4]));  // open: data
  ROM #(.addrWidth(4)) rom_3 (.addr(i_02[7:4]));  // open: data
  ROM #(.addrWidth(4)) rom_4 (.addr(i_03[7:4]));  // open: data
  Multiplexer #(.select(3), .width(5)) multiplexer_1 (
    .in0({1'b0, i_00[3:0]}), .in1({1'b0, i_01[3:0]}), .in2({1'b0, i_02[3:0]}), .in3({1'b0, i_03[3:0]}),
    .in4(5'b10000), .in5(5'b10000), .in6(5'b10000), .in7(5'b10000), .out(data), .sel(undriven));
  Multiplexer #(.select(3), .width(5)) multiplexer_2 (
    .in0({1'b0, i_00[3:0]}), .in1({1'b0, i_01[3:0]}), .in2({1'b0, i_02[3:0]}), .in3({1'b0, i_03[3:0]}),
    .in4(5'b10000), .in5(5'b10000), .in6(5'b10000), .in7(5'b10000), .out(arithm1));  // open: sel
  Multiplexer #(.select(3), .width(5)) multiplexer_3 (
    .in0({1'b0, i_00[3:0]}), .in1({1'b0, i_01[3:0]}), .in2({1'b0, i_02[3:0]}), .in3({1'b0, i_03[3:0]}),
    .in4(5'b10000), .in5(5'b10000), .in6(5'b10000), .in7(5'b10000), .out(arithm2));  // open: sel
  Multiplexer #(.select(3), .width(5)) multiplexer_4 (
    .in0({1'b0, i_00[3:0]}), .in1({1'b0, i_01[3:0]}), .in2({1'b0, i_02[3:0]}), .in3({1'b0, i_03[3:0]}),
    .in4(5'b10000), .in5(5'b10000), .in6(5'b10000), .in7(5'b10000), .out(ctrl));  // open: sel

  // Other names for the same wires on the sheet: first_instruction[3:0] = i_00[3:0];
  //   fourth_instruction[3:0] = i_03[3:0]; second_instruction[3:0] = i_01[3:0]; third_instruction[3:0] = i_02[3:0]
endmodule

module Selector_3bits (
  input  a,
  input  b,
  input  c,
  input  d,
  output [2:0] x
);

  wire not_1_out, not_2_out, not_3_out, not_4_out;

  not not_1 (not_1_out, a);
  not not_2 (not_2_out, b);
  not not_3 (not_3_out, c);
  not not_4 (not_4_out, d);
  and and_1 (x[2], not_1_out, not_2_out, not_3_out, not_4_out);
  or or_1 (x[1], d, c);
  or or_2 (x[0], d, b);
endmodule
